// Logisim project alarme-residencial.circ as structural Verilog: 8 circuits, main circuit main
module main (
  input  Y,
  input  I,
  input  J1,
  input  J2,
  input  J3,
  input  J4,
  input  P,
  output A
);

  wire and_1_out, and_2_out, and_3_out, and_4_out, and_5_out, and_6_out, and_7_out, and_8_out, and_9_out,
       and_10_out, and_11_out, and_12_out, and_13_out, button_1_out, button_2_out, button_3_out,
       button_4_out, button_5_out, button_6_out, button_7_out, button_8_out, clock_1_out,
       comparador_4bits_1_saida, comparador_4bits_2_saida, comparador_4bits_3_saida,
       comparador_4bits_4_saida, contador_decadico_1_dig_0, contador_decadico_1_dig_1,
       contador_decadico_1_dig_2, contador_decadico_1_dig_3, contador_decadico_2_dig_0,
       contador_decadico_2_dig_1, contador_decadico_2_dig_2, contador_decadico_2_dig_3,
       contador_decadico_3_dig_0, contador_decadico_3_dig_1, contador_decadico_3_dig_2,
       contador_decadico_3_dig_3, contador_decadico_4_dig_0, contador_decadico_4_dig_1,
       contador_decadico_4_dig_2, contador_decadico_4_dig_3, contador_decadico_5_dig_0,
       contador_decadico_5_dig_1, contador_decadico_5_dig_2, contador_decadico_5_dig_3,
       contador_decadico_6_dig_0, contador_decadico_6_dig_1, contador_decadico_6_dig_2,
       contador_decadico_6_dig_3, contador_decadico_7_dig_0, contador_decadico_7_dig_1,
       contador_decadico_7_dig_2, contador_decadico_7_dig_3, contador_decadico_8_dig_0,
       contador_decadico_8_dig_1, contador_decadico_8_dig_2, contador_decadico_8_dig_3,
       contador_mod2_1_saida, display_7segmentos_1_a, display_7segmentos_1_b, display_7segmentos_1_c,
       display_7segmentos_1_d, display_7segmentos_1_e, display_7segmentos_1_f, display_7segmentos_1_g,
       display_7segmentos_2_a, display_7segmentos_2_b, display_7segmentos_2_c, display_7segmentos_2_d,
       display_7segmentos_2_e, display_7segmentos_2_f, display_7segmentos_2_g, display_7segmentos_3_a,
       display_7segmentos_3_b, display_7segmentos_3_c, display_7segmentos_3_d, display_7segmentos_3_e,
       display_7segmentos_3_f, display_7segmentos_3_g, display_7segmentos_4_a, display_7segmentos_4_b,
       display_7segmentos_4_c, display_7segmentos_4_d, display_7segmentos_4_e, display_7segmentos_4_f,
       display_7segmentos_4_g, display_7segmentos_5_a, display_7segmentos_5_b, display_7segmentos_5_c,
       display_7segmentos_5_d, display_7segmentos_5_e, display_7segmentos_5_f, display_7segmentos_5_g,
       display_7segmentos_6_a, display_7segmentos_6_b, display_7segmentos_6_c, display_7segmentos_6_d,
       display_7segmentos_6_e, display_7segmentos_6_f, display_7segmentos_6_g, display_7segmentos_7_a,
       display_7segmentos_7_b, display_7segmentos_7_c, display_7segmentos_7_d, display_7segmentos_7_e,
       display_7segmentos_7_f, display_7segmentos_7_g, not_1_out, not_2_out, temporizador_3min_1_habilitador,
       temporizador_3min_1_out_5, temporizador_3min_1_out_6, temporizador_3min_1_out_7,
       temporizador_3min_1_out_8, temporizador_3min_1_out_9, temporizador_3min_1_out_10,
       temporizador_3min_1_out_11, temporizador_3min_1_out_12, temporizador_3min_1_out_13;

  contador_decadico contador_decadico_1 (
    .clock(button_1_out), .clear(and_5_out), .dig_3(contador_decadico_1_dig_3),
    .dig_2(contador_decadico_1_dig_2), .dig_1(contador_decadico_1_dig_1), .dig_0(contador_decadico_1_dig_0));
  Button button_1 (.out(button_1_out));
  contador_decadico contador_decadico_2 (
    .clock(button_2_out), .dig_3(contador_decadico_2_dig_3), .dig_2(contador_decadico_2_dig_2),
    .dig_1(contador_decadico_2_dig_1), .dig_0(contador_decadico_2_dig_0));  // open: clear
  Button button_2 (.out(button_2_out));
  _7_Segment_Display u_7_segment_display_1 (
    .g(display_7segmentos_1_g), .f(display_7segmentos_1_f), .a(display_7segmentos_1_a),
    .b(display_7segmentos_1_b), .e(display_7segmentos_1_e), .d(display_7segmentos_1_d),
    .c(display_7segmentos_1_c));  // open: dp
  display_7segmentos display_7segmentos_1 (
    .bin3(contador_decadico_1_dig_3), .bin2(contador_decadico_1_dig_2), .bin1(contador_decadico_1_dig_1),
    .bin0(contador_decadico_1_dig_0), .a(display_7segmentos_1_a), .b(display_7segmentos_1_b),
    .c(display_7segmentos_1_c), .d(display_7segmentos_1_d), .e(display_7segmentos_1_e),
    .f(display_7segmentos_1_f), .g(display_7segmentos_1_g));
  comparador_4bits comparador_4bits_1 (
    .A_3(contador_decadico_1_dig_3), .B_3(contador_decadico_2_dig_3), .A_2(contador_decadico_1_dig_2),
    .B_2(contador_decadico_2_dig_2), .A_1(contador_decadico_1_dig_1), .B_1(contador_decadico_2_dig_1),
    .A_0(contador_decadico_1_dig_0), .B_0(contador_decadico_2_dig_0), .saida(comparador_4bits_1_saida));
  contador_decadico contador_decadico_3 (
    .clock(button_3_out), .clear(and_5_out), .dig_3(contador_decadico_3_dig_3),
    .dig_2(contador_decadico_3_dig_2), .dig_1(contador_decadico_3_dig_1), .dig_0(contador_decadico_3_dig_0));
  Button button_3 (.out(button_3_out));
  and and_1 (and_1_out, ~contador_decadico_2_dig_3, ~contador_decadico_2_dig_2, ~contador_decadico_2_dig_1, ~contador_decadico_2_dig_0);  // AND_Gate
  display_7segmentos display_7segmentos_2 (
    .bin3(contador_decadico_3_dig_3), .bin2(contador_decadico_3_dig_2), .bin1(contador_decadico_3_dig_1),
    .bin0(contador_decadico_3_dig_0), .a(display_7segmentos_2_a), .b(display_7segmentos_2_b),
    .c(display_7segmentos_2_c), .d(display_7segmentos_2_d), .e(display_7segmentos_2_e),
    .f(display_7segmentos_2_f), .g(display_7segmentos_2_g));
  contador_decadico contador_decadico_4 (
    .clock(button_4_out), .dig_3(contador_decadico_4_dig_3), .dig_2(contador_decadico_4_dig_2),
    .dig_1(contador_decadico_4_dig_1), .dig_0(contador_decadico_4_dig_0));  // open: clear
  Button button_4 (.out(button_4_out));
  _7_Segment_Display u_7_segment_display_2 (
    .g(display_7segmentos_2_g), .f(display_7segmentos_2_f), .a(display_7segmentos_2_a),
    .b(display_7segmentos_2_b), .e(display_7segmentos_2_e), .d(display_7segmentos_2_d),
    .c(display_7segmentos_2_c));  // open: dp
  Button button_5 (.out(button_5_out));
  comparador_4bits comparador_4bits_2 (
    .A_3(contador_decadico_3_dig_3), .B_3(contador_decadico_4_dig_3), .A_2(contador_decadico_3_dig_2),
    .B_2(contador_decadico_4_dig_2), .A_1(contador_decadico_3_dig_1), .B_1(contador_decadico_4_dig_1),
    .A_0(contador_decadico_3_dig_0), .B_0(contador_decadico_4_dig_0), .saida(comparador_4bits_2_saida));
  contador_decadico contador_decadico_5 (
    .clock(button_5_out), .clear(and_5_out), .dig_3(contador_decadico_5_dig_3),
    .dig_2(contador_decadico_5_dig_2), .dig_1(contador_decadico_5_dig_1), .dig_0(contador_decadico_5_dig_0));
  Button button_6 (.out(button_6_out));
  and and_2 (and_2_out, ~contador_decadico_4_dig_3, ~contador_decadico_4_dig_2, ~contador_decadico_4_dig_1, ~contador_decadico_4_dig_0);  // AND_Gate
  display_7segmentos display_7segmentos_3 (
    .bin3(contador_decadico_5_dig_3), .bin2(contador_decadico_5_dig_2), .bin1(contador_decadico_5_dig_1),
    .bin0(contador_decadico_5_dig_0), .a(display_7segmentos_3_a), .b(display_7segmentos_3_b),
    .c(display_7segmentos_3_c), .d(display_7segmentos_3_d), .e(display_7segmentos_3_e),
    .f(display_7segmentos_3_f), .g(display_7segmentos_3_g));
  contador_decadico contador_decadico_6 (
    .clock(button_6_out), .dig_3(contador_decadico_6_dig_3), .dig_2(contador_decadico_6_dig_2),
    .dig_1(contador_decadico_6_dig_1), .dig_0(contador_decadico_6_dig_0));  // open: clear
  _7_Segment_Display u_7_segment_display_3 (
    .g(display_7segmentos_3_g), .f(display_7segmentos_3_f), .a(display_7segmentos_3_a),
    .b(display_7segmentos_3_b), .e(display_7segmentos_3_e), .d(display_7segmentos_3_d),
    .c(display_7segmentos_3_c));  // open: dp
  contador_decadico contador_decadico_7 (
    .clock(button_7_out), .clear(and_5_out), .dig_3(contador_decadico_7_dig_3),
    .dig_2(contador_decadico_7_dig_2), .dig_1(contador_decadico_7_dig_1), .dig_0(contador_decadico_7_dig_0));
  Button button_7 (.out(button_7_out));
  comparador_4bits comparador_4bits_3 (
    .A_3(contador_decadico_5_dig_3), .B_3(contador_decadico_6_dig_3), .A_2(contador_decadico_5_dig_2),
    .B_2(contador_decadico_6_dig_2), .A_1(contador_decadico_5_dig_1), .B_1(contador_decadico_6_dig_1),
    .A_0(contador_decadico_5_dig_0), .B_0(contador_decadico_6_dig_0), .saida(comparador_4bits_3_saida));
  contador_decadico contador_decadico_8 (
    .clock(button_8_out), .dig_3(contador_decadico_8_dig_3), .dig_2(contador_decadico_8_dig_2),
    .dig_1(contador_decadico_8_dig_1), .dig_0(contador_decadico_8_dig_0));  // open: clear
  Button button_8 (.out(button_8_out));
  and and_3 (and_3_out, ~contador_decadico_6_dig_3, ~contador_decadico_6_dig_2, ~contador_decadico_6_dig_1, ~contador_decadico_6_dig_0);  // AND_Gate
  display_7segmentos display_7segmentos_4 (
    .bin3(contador_decadico_7_dig_3), .bin2(contador_decadico_7_dig_2), .bin1(contador_decadico_7_dig_1),
    .bin0(contador_decadico_7_dig_0), .a(display_7segmentos_4_a), .b(display_7segmentos_4_b),
    .c(display_7segmentos_4_c), .d(display_7segmentos_4_d), .e(display_7segmentos_4_e),
    .f(display_7segmentos_4_f), .g(display_7segmentos_4_g));
  _7_Segment_Display u_7_segment_display_4 (
    .g(display_7segmentos_4_g), .f(display_7segmentos_4_f), .a(display_7segmentos_4_a),
    .b(display_7segmentos_4_b), .e(display_7segmentos_4_e), .d(display_7segmentos_4_d),
    .c(display_7segmentos_4_c));  // open: dp
  comparador_4bits comparador_4bits_4 (
    .A_3(contador_decadico_7_dig_3), .B_3(contador_decadico_8_dig_3), .A_2(contador_decadico_7_dig_2),
    .B_2(contador_decadico_8_dig_2), .A_1(contador_decadico_7_dig_1), .B_1(contador_decadico_8_dig_1),
    .A_0(contador_decadico_7_dig_0), .B_0(contador_decadico_8_dig_0), .saida(comparador_4bits_4_saida));
  and and_4 (and_4_out, ~contador_decadico_8_dig_3, ~contador_decadico_8_dig_2, ~contador_decadico_8_dig_1, ~contador_decadico_8_dig_0);  // AND_Gate
  and and_5 (and_5_out, comparador_4bits_4_saida, comparador_4bits_3_saida, comparador_4bits_2_saida, comparador_4bits_1_saida);
  and and_6 (and_6_out, and_4_out, and_3_out, and_2_out, and_1_out);
  not not_1 (not_1_out, contador_mod2_1_saida);
  contador_mod2 contador_mod2_1 (.clock(and_5_out), .clear(and_6_out), .saida(contador_mod2_1_saida));
  Clock clock_1 (.out(clock_1_out));
  display_7segmentos display_7segmentos_5 (
    .bin3(1'b0), .bin2(1'b0), .bin1(temporizador_3min_1_out_5), .bin0(temporizador_3min_1_out_6),
    .a(display_7segmentos_5_a), .b(display_7segmentos_5_b), .c(display_7segmentos_5_c),
    .d(display_7segmentos_5_d), .e(display_7segmentos_5_e), .f(display_7segmentos_5_f),
    .g(display_7segmentos_5_g));
  and and_7 (and_7_out, clock_1_out, contador_mod2_1_saida);
  _7_Segment_Display u_7_segment_display_5 (
    .g(display_7segmentos_5_g), .f(display_7segmentos_5_f), .a(display_7segmentos_5_a),
    .b(display_7segmentos_5_b), .e(display_7segmentos_5_e), .d(display_7segmentos_5_d),
    .c(display_7segmentos_5_c));  // open: dp
  temporizador_3min temporizador_3min_1 (
    .clock(and_7_out), .clear1(not_1_out), .clear2(not_1_out), .clear3(not_1_out),
    .out_10(temporizador_3min_1_out_10), .out_11(temporizador_3min_1_out_11),
    .out_12(temporizador_3min_1_out_12), .out_13(temporizador_3min_1_out_13),
    .out_7(temporizador_3min_1_out_7), .out_8(temporizador_3min_1_out_8), .out_9(temporizador_3min_1_out_9),
    .out_5(temporizador_3min_1_out_5), .out_6(temporizador_3min_1_out_6),
    .habilitador(temporizador_3min_1_habilitador));
  display_7segmentos display_7segmentos_6 (
    .bin3(1'b0), .bin2(temporizador_3min_1_out_7), .bin1(temporizador_3min_1_out_8),
    .bin0(temporizador_3min_1_out_9), .a(display_7segmentos_6_a), .b(display_7segmentos_6_b),
    .c(display_7segmentos_6_c), .d(display_7segmentos_6_d), .e(display_7segmentos_6_e),
    .f(display_7segmentos_6_f), .g(display_7segmentos_6_g));
  _7_Segment_Display u_7_segment_display_6 (
    .g(display_7segmentos_6_g), .f(display_7segmentos_6_f), .a(display_7segmentos_6_a),
    .b(display_7segmentos_6_b), .e(display_7segmentos_6_e), .d(display_7segmentos_6_d),
    .c(display_7segmentos_6_c));  // open: dp
  display_7segmentos display_7segmentos_7 (
    .bin3(temporizador_3min_1_out_10), .bin2(temporizador_3min_1_out_11), .bin1(temporizador_3min_1_out_12),
    .bin0(temporizador_3min_1_out_13), .a(display_7segmentos_7_a), .b(display_7segmentos_7_b),
    .c(display_7segmentos_7_c), .d(display_7segmentos_7_d), .e(display_7segmentos_7_e),
    .f(display_7segmentos_7_f), .g(display_7segmentos_7_g));
  _7_Segment_Display u_7_segment_display_7 (
    .g(display_7segmentos_7_g), .f(display_7segmentos_7_f), .a(display_7segmentos_7_a),
    .b(display_7segmentos_7_b), .e(display_7segmentos_7_e), .d(display_7segmentos_7_d),
    .c(display_7segmentos_7_c));  // open: dp
  and and_8 (and_8_out, temporizador_3min_1_habilitador, not_2_out, I);
  not not_2 (not_2_out, Y);
  and and_9 (and_9_out, temporizador_3min_1_habilitador, Y, P);
  and and_10 (and_10_out, temporizador_3min_1_habilitador, Y, J4);
  and and_11 (and_11_out, temporizador_3min_1_habilitador, Y, J3);
  and and_12 (and_12_out, temporizador_3min_1_habilitador, Y, J2);
  and and_13 (and_13_out, temporizador_3min_1_habilitador, Y, J1);
  or or_1 (A, and_8_out, and_9_out, and_10_out, and_11_out, and_12_out, and_13_out);
endmodule

module comparador_4bits (
  input  A_3,
  input  B_3,
  input  A_2,
  input  B_2,
  input  A_1,
  input  B_1,
  input  A_0,
  input  B_0,
  output saida
);

  wire and_1_out, and_2_out, xnor_1_out, xnor_2_out, xnor_3_out, xnor_4_out;

  xnor xnor_1 (xnor_1_out, A_3, B_3);
  xnor xnor_2 (xnor_2_out, A_2, B_2);
  xnor xnor_3 (xnor_3_out, A_1, B_1);
  xnor xnor_4 (xnor_4_out, A_0, B_0);
  and and_1 (and_1_out, xnor_1_out, xnor_2_out);
  and and_2 (and_2_out, xnor_3_out, xnor_4_out);
  and and_3 (saida, and_1_out, and_2_out);
endmodule

module entrada_senha (
  output out_1
);

  wire and_1_out, and_2_out, and_3_out, and_4_out, and_5_out, and_6_out, and_7_out, button_1_out,
       button_2_out, button_3_out, button_4_out, button_5_out, button_6_out, button_7_out, button_8_out,
       clock_1_out, comparador_4bits_1_saida, comparador_4bits_2_saida, comparador_4bits_3_saida,
       comparador_4bits_4_saida, contador_decadico_1_dig_0, contador_decadico_1_dig_1,
       contador_decadico_1_dig_2, contador_decadico_1_dig_3, contador_decadico_2_dig_0,
       contador_decadico_2_dig_1, contador_decadico_2_dig_2, contador_decadico_2_dig_3,
       contador_decadico_3_dig_0, contador_decadico_3_dig_1, contador_decadico_3_dig_2,
       contador_decadico_3_dig_3, contador_decadico_4_dig_0, contador_decadico_4_dig_1,
       contador_decadico_4_dig_2, contador_decadico_4_dig_3, contador_decadico_5_dig_0,
       contador_decadico_5_dig_1, contador_decadico_5_dig_2, contador_decadico_5_dig_3,
       contador_decadico_6_dig_0, contador_decadico_6_dig_1, contador_decadico_6_dig_2,
       contador_decadico_6_dig_3, contador_decadico_7_dig_0, contador_decadico_7_dig_1,
       contador_decadico_7_dig_2, contador_decadico_7_dig_3, contador_decadico_8_dig_0,
       contador_decadico_8_dig_1, contador_decadico_8_dig_2, contador_decadico_8_dig_3,
       contador_mod2_1_saida, display_7segmentos_1_a, display_7segmentos_1_b, display_7segmentos_1_c,
       display_7segmentos_1_d, display_7segmentos_1_e, display_7segmentos_1_f, display_7segmentos_1_g,
       display_7segmentos_2_a, display_7segmentos_2_b, display_7segmentos_2_c, display_7segmentos_2_d,
       display_7segmentos_2_e, display_7segmentos_2_f, display_7segmentos_2_g, display_7segmentos_3_a,
       display_7segmentos_3_b, display_7segmentos_3_c, display_7segmentos_3_d, display_7segmentos_3_e,
       display_7segmentos_3_f, display_7segmentos_3_g, display_7segmentos_4_a, display_7segmentos_4_b,
       display_7segmentos_4_c, display_7segmentos_4_d, display_7segmentos_4_e, display_7segmentos_4_f,
       display_7segmentos_4_g, display_7segmentos_5_a, display_7segmentos_5_b, display_7segmentos_5_c,
       display_7segmentos_5_d, display_7segmentos_5_e, display_7segmentos_5_f, display_7segmentos_5_g,
       display_7segmentos_6_a, display_7segmentos_6_b, display_7segmentos_6_c, display_7segmentos_6_d,
       display_7segmentos_6_e, display_7segmentos_6_f, display_7segmentos_6_g, display_7segmentos_7_a,
       display_7segmentos_7_b, display_7segmentos_7_c, display_7segmentos_7_d, display_7segmentos_7_e,
       display_7segmentos_7_f, display_7segmentos_7_g, not_1_out, temporizador_3min_1_out_5,
       temporizador_3min_1_out_6, temporizador_3min_1_out_7, temporizador_3min_1_out_8,
       temporizador_3min_1_out_9, temporizador_3min_1_out_10, temporizador_3min_1_out_11,
       temporizador_3min_1_out_12, temporizador_3min_1_out_13;

  contador_decadico contador_decadico_1 (
    .clock(button_1_out), .clear(and_5_out), .dig_3(contador_decadico_1_dig_3),
    .dig_2(contador_decadico_1_dig_2), .dig_1(contador_decadico_1_dig_1), .dig_0(contador_decadico_1_dig_0));
  Button button_1 (.out(button_1_out));
  contador_decadico contador_decadico_2 (
    .clock(button_2_out), .dig_3(contador_decadico_2_dig_3), .dig_2(contador_decadico_2_dig_2),
    .dig_1(contador_decadico_2_dig_1), .dig_0(contador_decadico_2_dig_0));  // open: clear
  Button button_2 (.out(button_2_out));
  _7_Segment_Display u_7_segment_display_1 (
    .g(display_7segmentos_1_g), .f(display_7segmentos_1_f), .a(display_7segmentos_1_a),
    .b(display_7segmentos_1_b), .e(display_7segmentos_1_e), .d(display_7segmentos_1_d),
    .c(display_7segmentos_1_c));  // open: dp
  display_7segmentos display_7segmentos_1 (
    .bin3(contador_decadico_1_dig_3), .bin2(contador_decadico_1_dig_2), .bin1(contador_decadico_1_dig_1),
    .bin0(contador_decadico_1_dig_0), .a(display_7segmentos_1_a), .b(display_7segmentos_1_b),
    .c(display_7segmentos_1_c), .d(display_7segmentos_1_d), .e(display_7segmentos_1_e),
    .f(display_7segmentos_1_f), .g(display_7segmentos_1_g));
  comparador_4bits comparador_4bits_1 (
    .A_3(contador_decadico_1_dig_3), .B_3(contador_decadico_2_dig_3), .A_2(contador_decadico_1_dig_2),
    .B_2(contador_decadico_2_dig_2), .A_1(contador_decadico_1_dig_1), .B_1(contador_decadico_2_dig_1),
    .A_0(contador_decadico_1_dig_0), .B_0(contador_decadico_2_dig_0), .saida(comparador_4bits_1_saida));
  contador_decadico contador_decadico_3 (
    .clock(button_3_out), .clear(and_5_out), .dig_3(contador_decadico_3_dig_3),
    .dig_2(contador_decadico_3_dig_2), .dig_1(contador_decadico_3_dig_1), .dig_0(contador_decadico_3_dig_0));
  Button button_3 (.out(button_3_out));
  and and_1 (and_1_out, ~contador_decadico_2_dig_3, ~contador_decadico_2_dig_2, ~contador_decadico_2_dig_1, ~contador_decadico_2_dig_0);  // AND_Gate
  display_7segmentos display_7segmentos_2 (
    .bin3(contador_decadico_3_dig_3), .bin2(contador_decadico_3_dig_2), .bin1(contador_decadico_3_dig_1),
    .bin0(contador_decadico_3_dig_0), .a(display_7segmentos_2_a), .b(display_7segmentos_2_b),
    .c(display_7segmentos_2_c), .d(display_7segmentos_2_d), .e(display_7segmentos_2_e),
    .f(display_7segmentos_2_f), .g(display_7segmentos_2_g));
  contador_decadico contador_decadico_4 (
    .clock(button_4_out), .dig_3(contador_decadico_4_dig_3), .dig_2(contador_decadico_4_dig_2),
    .dig_1(contador_decadico_4_dig_1), .dig_0(contador_decadico_4_dig_0));  // open: clear
  Button button_4 (.out(button_4_out));
  _7_Segment_Display u_7_segment_display_2 (
    .g(display_7segmentos_2_g), .f(display_7segmentos_2_f), .a(display_7segmentos_2_a),
    .b(display_7segmentos_2_b), .e(display_7segmentos_2_e), .d(display_7segmentos_2_d),
    .c(display_7segmentos_2_c));  // open: dp
  Button button_5 (.out(button_5_out));
  comparador_4bits comparador_4bits_2 (
    .A_3(contador_decadico_3_dig_3), .B_3(contador_decadico_4_dig_3), .A_2(contador_decadico_3_dig_2),
    .B_2(contador_decadico_4_dig_2), .A_1(contador_decadico_3_dig_1), .B_1(contador_decadico_4_dig_1),
    .A_0(contador_decadico_3_dig_0), .B_0(contador_decadico_4_dig_0), .saida(comparador_4bits_2_saida));
  contador_decadico contador_decadico_5 (
    .clock(button_5_out), .clear(and_5_out), .dig_3(contador_decadico_5_dig_3),
    .dig_2(contador_decadico_5_dig_2), .dig_1(contador_decadico_5_dig_1), .dig_0(contador_decadico_5_dig_0));
  Button button_6 (.out(button_6_out));
  and and_2 (and_2_out, ~contador_decadico_4_dig_3, ~contador_decadico_4_dig_2, ~contador_decadico_4_dig_1, ~contador_decadico_4_dig_0);  // AND_Gate
  display_7segmentos display_7segmentos_3 (
    .bin3(contador_decadico_5_dig_3), .bin2(contador_decadico_5_dig_2), .bin1(contador_decadico_5_dig_1),
    .bin0(contador_decadico_5_dig_0), .a(display_7segmentos_3_a), .b(display_7segmentos_3_b),
    .c(display_7segmentos_3_c), .d(display_7segmentos_3_d), .e(display_7segmentos_3_e),
    .f(display_7segmentos_3_f), .g(display_7segmentos_3_g));
  contador_decadico contador_decadico_6 (
    .clock(button_6_out), .dig_3(contador_decadico_6_dig_3), .dig_2(contador_decadico_6_dig_2),
    .dig_1(contador_decadico_6_dig_1), .dig_0(contador_decadico_6_dig_0));  // open: clear
  _7_Segment_Display u_7_segment_display_3 (
    .g(display_7segmentos_3_g), .f(display_7segmentos_3_f), .a(display_7segmentos_3_a),
    .b(display_7segmentos_3_b), .e(display_7segmentos_3_e), .d(display_7segmentos_3_d),
    .c(display_7segmentos_3_c));  // open: dp
  contador_decadico contador_decadico_7 (
    .clock(button_7_out), .clear(and_5_out), .dig_3(contador_decadico_7_dig_3),
    .dig_2(contador_decadico_7_dig_2), .dig_1(contador_decadico_7_dig_1), .dig_0(contador_decadico_7_dig_0));
  Button button_7 (.out(button_7_out));
  comparador_4bits comparador_4bits_3 (
    .A_3(contador_decadico_5_dig_3), .B_3(contador_decadico_6_dig_3), .A_2(contador_decadico_5_dig_2),
    .B_2(contador_decadico_6_dig_2), .A_1(contador_decadico_5_dig_1), .B_1(contador_decadico_6_dig_1),
    .A_0(contador_decadico_5_dig_0), .B_0(contador_decadico_6_dig_0), .saida(comparador_4bits_3_saida));
  contador_decadico contador_decadico_8 (
    .clock(button_8_out), .dig_3(contador_decadico_8_dig_3), .dig_2(contador_decadico_8_dig_2),
    .dig_1(contador_decadico_8_dig_1), .dig_0(contador_decadico_8_dig_0));  // open: clear
  Button button_8 (.out(button_8_out));
  and and_3 (and_3_out, ~contador_decadico_6_dig_3, ~contador_decadico_6_dig_2, ~contador_decadico_6_dig_1, ~contador_decadico_6_dig_0);  // AND_Gate
  display_7segmentos display_7segmentos_4 (
    .bin3(contador_decadico_7_dig_3), .bin2(contador_decadico_7_dig_2), .bin1(contador_decadico_7_dig_1),
    .bin0(contador_decadico_7_dig_0), .a(display_7segmentos_4_a), .b(display_7segmentos_4_b),
    .c(display_7segmentos_4_c), .d(display_7segmentos_4_d), .e(display_7segmentos_4_e),
    .f(display_7segmentos_4_f), .g(display_7segmentos_4_g));
  _7_Segment_Display u_7_segment_display_4 (
    .g(display_7segmentos_4_g), .f(display_7segmentos_4_f), .a(display_7segmentos_4_a),
    .b(display_7segmentos_4_b), .e(display_7segmentos_4_e), .d(display_7segmentos_4_d),
    .c(display_7segmentos_4_c));  // open: dp
  comparador_4bits comparador_4bits_4 (
    .A_3(contador_decadico_7_dig_3), .B_3(contador_decadico_8_dig_3), .A_2(contador_decadico_7_dig_2),
    .B_2(contador_decadico_8_dig_2), .A_1(contador_decadico_7_dig_1), .B_1(contador_decadico_8_dig_1),
    .A_0(contador_decadico_7_dig_0), .B_0(contador_decadico_8_dig_0), .saida(comparador_4bits_4_saida));
  and and_4 (and_4_out, ~contador_decadico_8_dig_3, ~contador_decadico_8_dig_2, ~contador_decadico_8_dig_1, ~contador_decadico_8_dig_0);  // AND_Gate
  and and_5 (and_5_out, comparador_4bits_4_saida, comparador_4bits_3_saida, comparador_4bits_2_saida, comparador_4bits_1_saida);
  and and_6 (and_6_out, and_4_out, and_3_out, and_2_out, and_1_out);
  contador_mod2 contador_mod2_1 (.clock(and_5_out), .clear(and_6_out), .saida(contador_mod2_1_saida));
  not not_1 (not_1_out, contador_mod2_1_saida);
  Clock clock_1 (.out(clock_1_out));
  display_7segmentos display_7segmentos_5 (
    .bin3(1'b0), .bin2(1'b0), .bin1(temporizador_3min_1_out_5), .bin0(temporizador_3min_1_out_6),
    .a(display_7segmentos_5_a), .b(display_7segmentos_5_b), .c(display_7segmentos_5_c),
    .d(display_7segmentos_5_d), .e(display_7segmentos_5_e), .f(display_7segmentos_5_f),
    .g(display_7segmentos_5_g));
  and and_7 (and_7_out, clock_1_out, contador_mod2_1_saida);
  _7_Segment_Display u_7_segment_display_5 (
    .g(display_7segmentos_5_g), .f(display_7segmentos_5_f), .a(display_7segmentos_5_a),
    .b(display_7segmentos_5_b), .e(display_7segmentos_5_e), .d(display_7segmentos_5_d),
    .c(display_7segmentos_5_c));  // open: dp
  temporizador_3min temporizador_3min_1 (
    .clock(and_7_out), .clear1(not_1_out), .clear2(not_1_out), .clear3(not_1_out),
    .out_10(temporizador_3min_1_out_10), .out_11(temporizador_3min_1_out_11),
    .out_12(temporizador_3min_1_out_12), .out_13(temporizador_3min_1_out_13),
    .out_7(temporizador_3min_1_out_7), .out_8(temporizador_3min_1_out_8), .out_9(temporizador_3min_1_out_9),
    .out_5(temporizador_3min_1_out_5), .out_6(temporizador_3min_1_out_6), .habilitador(out_1));
  display_7segmentos display_7segmentos_6 (
    .bin3(1'b0), .bin2(temporizador_3min_1_out_7), .bin1(temporizador_3min_1_out_8),
    .bin0(temporizador_3min_1_out_9), .a(display_7segmentos_6_a), .b(display_7segmentos_6_b),
    .c(display_7segmentos_6_c), .d(display_7segmentos_6_d), .e(display_7segmentos_6_e),
    .f(display_7segmentos_6_f), .g(display_7segmentos_6_g));
  _7_Segment_Display u_7_segment_display_6 (
    .g(display_7segmentos_6_g), .f(display_7segmentos_6_f), .a(display_7segmentos_6_a),
    .b(display_7segmentos_6_b), .e(display_7segmentos_6_e), .d(display_7segmentos_6_d),
    .c(display_7segmentos_6_c));  // open: dp
  _7_Segment_Display u_7_segment_display_7 (
    .g(display_7segmentos_7_g), .f(display_7segmentos_7_f), .a(display_7segmentos_7_a),
    .b(display_7segmentos_7_b), .e(display_7segmentos_7_e), .d(display_7segmentos_7_d),
    .c(display_7segmentos_7_c));  // open: dp
  display_7segmentos display_7segmentos_7 (
    .bin3(temporizador_3min_1_out_10), .bin2(temporizador_3min_1_out_11), .bin1(temporizador_3min_1_out_12),
    .bin0(temporizador_3min_1_out_13), .a(display_7segmentos_7_a), .b(display_7segmentos_7_b),
    .c(display_7segmentos_7_c), .d(display_7segmentos_7_d), .e(display_7segmentos_7_e),
    .f(display_7segmentos_7_f), .g(display_7segmentos_7_g));
endmodule

module temporizador_3min (
  input  clock,
  input  clear1,
  input  clear2,
  input  clear3,
  output out_5,
  output out_6,
  output out_7,
  output out_8,
  output out_9,
  output out_10,
  output out_11,
  output out_12,
  output out_13,
  output habilitador
);

  wire and_1_out, and_2_out, and_3_out, and_4_out, and_5_out, and_6_out, or_1_out, or_2_out, or_3_out;

  and and_1 (and_1_out, out_13, out_12, out_11);
  J_K_Flip_Flop #(.trigger("falling")) j_k_ff_1 (
    .J(and_1_out), .clk(clock), .K(and_1_out), .Q(out_10), .reset(or_1_out));  // open: Qn, preset, en
  and and_2 (and_2_out, out_13, out_12);
  J_K_Flip_Flop #(.trigger("falling")) j_k_ff_2 (
    .J(and_2_out), .clk(clock), .K(and_2_out), .Q(out_11), .reset(or_1_out));  // open: Qn, preset, en
  J_K_Flip_Flop #(.trigger("falling")) j_k_ff_3 (
    .J(out_13), .clk(clock), .K(out_13), .Q(out_12), .reset(or_1_out));  // open: Qn, preset, en
  and and_3 (and_3_out, out_10, out_12);
  J_K_Flip_Flop #(.trigger("falling")) j_k_ff_4 (
    .J(1'b1), .clk(clock), .K(1'b1), .Q(out_13), .reset(or_1_out));  // open: Qn, preset, en
  or or_1 (or_1_out, and_3_out, habilitador, clear1);
  and and_4 (and_4_out, out_9, out_8);
  J_K_Flip_Flop #(.trigger("falling")) j_k_ff_5 (
    .J(and_4_out), .clk(and_3_out), .K(and_4_out), .Q(out_7), .reset(or_2_out));  // open: Qn, preset, en
  J_K_Flip_Flop #(.trigger("falling")) j_k_ff_6 (
    .J(out_9), .clk(and_3_out), .K(out_9), .Q(out_8), .reset(or_2_out));  // open: Qn, preset, en
  J_K_Flip_Flop #(.trigger("falling")) j_k_ff_7 (
    .J(1'b1), .clk(and_3_out), .K(1'b1), .Q(out_9), .reset(or_2_out));  // open: Qn, preset, en
  and and_5 (and_5_out, out_8, out_7);
  or or_2 (or_2_out, and_5_out, habilitador, clear2);
  J_K_Flip_Flop #(.trigger("falling")) j_k_ff_8 (
    .J(out_6), .clk(and_5_out), .K(out_6), .Q(out_5), .reset(or_3_out));  // open: Qn, preset, en
  J_K_Flip_Flop #(.trigger("falling")) j_k_ff_9 (
    .J(1'b1), .clk(and_5_out), .K(1'b1), .Q(out_6), .reset(or_3_out));  // open: Qn, preset, en
  and and_6 (and_6_out, out_6, out_5);
  or or_3 (or_3_out, and_6_out, habilitador, clear3);
  contador_mod2 contador_mod2_1 (.clock(and_6_out), .clear(clear3), .saida(habilitador));
endmodule

module contador_decadico (
  input  clock,
  input  clear,
  output dig_3,
  output dig_2,
  output dig_1,
  output dig_0
);

  wire and_1_out, and_2_out, and_3_out, or_1_out;

  and and_1 (and_1_out, dig_0, dig_1, dig_2);
  J_K_Flip_Flop #(.trigger("falling")) j_k_ff_1 (
    .J(and_1_out), .clk(clock), .K(and_1_out), .Q(dig_3), .reset(or_1_out));  // open: Qn, preset, en
  and and_2 (and_2_out, dig_0, dig_1);
  J_K_Flip_Flop #(.trigger("falling")) j_k_ff_2 (
    .J(and_2_out), .clk(clock), .K(and_2_out), .Q(dig_2), .reset(or_1_out));  // open: Qn, preset, en
  J_K_Flip_Flop #(.trigger("falling")) j_k_ff_3 (
    .J(dig_0), .clk(clock), .K(dig_0), .Q(dig_1), .reset(or_1_out));  // open: Qn, preset, en
  J_K_Flip_Flop #(.trigger("falling")) j_k_ff_4 (
    .J(1'b1), .clk(clock), .K(1'b1), .Q(dig_0), .reset(or_1_out));  // open: Qn, preset, en
  and and_3 (and_3_out, dig_3, dig_1);
  or or_1 (or_1_out, and_3_out, clear);
endmodule

module display_7segmentos (
  input  bin3,
  input  bin2,
  input  bin1,
  input  bin0,
  output a,
  output b,
  output c,
  output d,
  output e,
  output f,
  output g
);

  wire and_1_out, and_2_out, and_3_out, and_4_out, and_5_out, and_6_out, and_7_out, and_8_out, and_9_out,
       and_10_out, and_11_out, and_12_out, and_13_out, and_14_out, and_15_out, and_16_out, and_17_out,
       and_18_out, and_19_out, and_20_out, and_21_out, and_22_out, and_23_out, and_24_out, and_25_out,
       not_1_out, not_2_out, not_3_out, not_4_out, not_5_out, not_6_out, not_7_out, not_8_out, not_9_out,
       not_10_out, not_11_out, not_12_out, not_13_out, not_14_out, not_15_out, not_16_out, not_17_out,
       not_18_out, not_19_out, not_20_out, not_21_out, not_22_out, not_23_out, not_24_out, not_25_out,
       not_26_out, not_27_out, not_28_out, not_29_out, not_30_out, not_31_out, not_32_out, not_33_out,
       not_34_out, not_35_out, not_36_out, not_37_out, not_38_out, not_39_out, not_40_out, not_41_out,
       not_42_out, not_43_out, not_44_out, not_45_out, not_46_out, not_47_out;

  not not_1 (not_1_out, bin3);
  not not_2 (not_2_out, bin2);
  and and_1 (and_1_out, not_1_out, not_2_out, not_3_out);
  not not_3 (not_3_out, bin0);
  not not_4 (not_4_out, bin3);
  and and_2 (and_2_out, not_4_out, bin1);
  not not_5 (not_5_out, bin3);
  and and_3 (and_3_out, not_5_out, bin2, bin0);
  not not_6 (not_6_out, bin2);
  and and_4 (and_4_out, bin3, not_6_out, not_7_out);
  not not_7 (not_7_out, bin1);
  not not_8 (not_8_out, bin3);
  and and_5 (and_5_out, not_8_out, not_9_out);
  not not_9 (not_9_out, bin2);
  not not_10 (not_10_out, bin3);
  not not_11 (not_11_out, bin1);
  and and_6 (and_6_out, not_10_out, not_11_out, not_12_out);
  not not_12 (not_12_out, bin0);
  not not_13 (not_13_out, bin2);
  and and_7 (and_7_out, not_13_out, not_14_out);
  not not_14 (not_14_out, bin1);
  not not_15 (not_15_out, bin3);
  and and_8 (and_8_out, not_15_out, bin1, bin0);
  not not_16 (not_16_out, bin2);
  and and_9 (and_9_out, not_16_out, not_17_out);
  not not_17 (not_17_out, bin1);
  not not_18 (not_18_out, bin3);
  and and_10 (and_10_out, not_18_out, bin0);
  not not_19 (not_19_out, bin3);
  and and_11 (and_11_out, not_19_out, bin2);
  not not_20 (not_20_out, bin3);
  not not_21 (not_21_out, bin2);
  not not_22 (not_22_out, bin0);
  not not_23 (not_23_out, bin3);
  not not_24 (not_24_out, bin2);
  not not_25 (not_25_out, bin3);
  not not_26 (not_26_out, bin0);
  not not_27 (not_27_out, bin3);
  not not_28 (not_28_out, bin1);
  not not_29 (not_29_out, bin2);
  not not_30 (not_30_out, bin1);
  not not_31 (not_31_out, bin2);
  and and_12 (and_12_out, not_31_out, not_32_out, not_33_out);
  not not_32 (not_32_out, bin1);
  not not_33 (not_33_out, bin0);
  not not_34 (not_34_out, bin3);
  and and_13 (and_13_out, not_34_out, bin1, not_35_out);
  not not_35 (not_35_out, bin0);
  not not_36 (not_36_out, bin3);
  not not_37 (not_37_out, bin1);
  and and_14 (and_14_out, not_36_out, not_37_out, not_38_out);
  not not_38 (not_38_out, bin0);
  not not_39 (not_39_out, bin3);
  and and_15 (and_15_out, not_39_out, bin2, not_40_out);
  not not_40 (not_40_out, bin1);
  not not_41 (not_41_out, bin3);
  and and_16 (and_16_out, not_41_out, bin2, not_42_out);
  not not_42 (not_42_out, bin0);
  not not_43 (not_43_out, bin2);
  and and_17 (and_17_out, bin3, not_43_out, not_44_out);
  not not_44 (not_44_out, bin1);
  not not_45 (not_45_out, bin2);
  and and_18 (and_18_out, not_45_out, bin1);
  and and_19 (and_19_out, bin2, not_46_out);
  not not_46 (not_46_out, bin1);
  and and_20 (and_20_out, bin2, not_47_out);
  not not_47 (not_47_out, bin0);
  or or_1 (a, and_1_out, and_2_out, and_3_out, and_4_out);
  or or_2 (b, and_5_out, and_6_out, and_7_out, and_8_out);
  or or_3 (c, and_9_out, and_10_out, and_11_out);
  and and_21 (and_21_out, not_20_out, not_21_out, not_22_out);
  and and_22 (and_22_out, not_23_out, not_24_out, bin1);
  and and_23 (and_23_out, not_25_out, bin1, not_26_out);
  and and_24 (and_24_out, not_27_out, bin2, not_28_out, bin0);
  and and_25 (and_25_out, bin3, not_29_out, not_30_out);
  or or_4 (e, and_12_out, and_13_out);
  or or_5 (f, and_14_out, and_15_out, and_16_out, and_17_out);
  or or_6 (g, and_18_out, and_19_out, and_20_out, bin3);
  or or_7 (d, and_21_out, and_22_out, and_23_out, and_24_out, and_25_out);
endmodule

module contador_mod2 (
  input  clock,
  input  clear,
  output saida
);

  J_K_Flip_Flop j_k_ff_1 (.J(1'b1), .clk(clock), .K(1'b1), .Q(saida), .reset(clear));  // open: Qn, preset, en
endmodule

module alarme_detector (
  input  habilitador,
  input  Y,
  input  I,
  input  J1,
  input  J2,
  input  J3,
  input  J4,
  input  P,
  output A
);

  wire and_1_out, and_2_out, and_3_out, and_4_out, and_5_out, and_6_out, not_1_out;

  not not_1 (not_1_out, Y);
  and and_1 (and_1_out, habilitador, not_1_out, I);
  and and_2 (and_2_out, habilitador, Y, P);
  and and_3 (and_3_out, habilitador, Y, J4);
  and and_4 (and_4_out, habilitador, Y, J3);
  and and_5 (and_5_out, habilitador, Y, J2);
  and and_6 (and_6_out, habilitador, Y, J1);
  or or_1 (A, and_1_out, and_2_out, and_3_out, and_4_out, and_5_out, and_6_out);
endmodule
